# Fritzing sketch diagrama TB-1 (saved by Fritzing 0.9.2b)

parts:
  Parte1 = Arduino Nano (Rev3.0)
  LCD1 = LCD screen
  LCM1602_IIC1 = LCM1602 IIC [part_number="LCM1602 IIC" chip_label="LCM1602 IIC" package="DIP (Dual Inline) [THT]"]
  DHT11 = Humidity and Temperature Sensor RHT03
  R1 = Resistor [tolerance=±5% resistance=10k package=THT]
  Selector_de_temperatura = Rotary Potentiometer (Small) [maximum_resistance=100kΩ package=THT]
  Selector_de_margen = Rotary Potentiometer (Small) [maximum_resistance=100kΩ package=THT]
  Sonda_temperatura = DS18B20 1-Wire Temperature Sensor [part_number=DS18B20]
  R2 = Resistor [tolerance=±5% resistance=4.7 package=THT]
  Relé_Calor = Keyes Relay [package=THT]
  Relé_Frío = Keyes Relay [package=THT]
  12V = Power plug

nets:
  GND: Parte1.GND, LCM1602_IIC1.GND, DHT11.GND_2, 12V.GND
  N1: Parte1.D2, Sonda_temperatura.DQ, R2.Pin_0
  N2: Parte1.D4, DHT11.Data-signal, R1.Pin_1
  N3: Parte1.D5, Relé_Frío.signal
  N4: Parte1.D6, Relé_Calor.signal
  VIN: Parte1.VIN, 12V.VCC
  VCC: Parte1.5V, LCM1602_IIC1.VCC, DHT11.Vcc, R1.Pin_0
  N5: Parte1.A5, LCM1602_IIC1.SCL
  N6: Parte1.A4, LCM1602_IIC1.SDA
  N7: Parte1.A1, Selector_de_temperatura.wiper
  N8: Parte1.A0, Selector_de_margen.wiper
  VSS: LCD1.VSS, LCM1602_IIC1.VSS
  VDD: LCD1.VDD, LCM1602_IIC1.VDD
  N9: LCD1.V0, LCM1602_IIC1.V0
  N10: LCD1.RS, LCM1602_IIC1.RS
  N11: LCD1.R/W, LCM1602_IIC1.RW
  N12: LCD1.E, LCM1602_IIC1.E
  N13: LCD1.DB0, LCM1602_IIC1.D0
  N14: LCD1.DB1, LCM1602_IIC1.D1
  N15: LCD1.DB2, LCM1602_IIC1.D2
  N16: LCD1.DB3, LCM1602_IIC1.D3
  N17: LCD1.DB4, LCM1602_IIC1.D4
  N18: LCD1.DB5, LCM1602_IIC1.D5
  N19: LCD1.DB6, LCM1602_IIC1.D6
  N20: LCD1.DB7, LCM1602_IIC1.D7
  N21: LCD1.LED+, LCM1602_IIC1.A
  N22: LCD1.LED-, LCM1602_IIC1.K

notes:
  Los sensores DHT encapsulados, ya llevan la resistencia incorporada y solo tienen 3 pines, por lo que la conexion sería igual pero sin incluir la resistencia; se conectaría cada patilla directamente al conector de arduino necesario.
  El valor de los potenciometros no importa mucho. Yo uso de 20K porque son los que tenía a mano
  La sonda que yo uso viene encapsulada en goma con una punta de inox, pero la conexión es la misma
  En caso de usar relés SSR la toma de 5V no sería necesaria, por lo que se puede ignorar el cable rojo de los reles.
  El arduino usado es un Arduino Nano (copia china), por ser pequeño y barato, pero puede usarse cualquier modelo de arduino.

custom parts:
  LCM1602 IIC: I2C-Module to use a 1602 or 2004 LCD on with the wire.h libory Serial LCD Modul
  Keyes Relay: The Keyes 5V relay module is suitable for SCM development, home appliance control. It uses a 5V~12V TIL control signal which can control DC / AC signal.
